// Digital circuit control.dig as structural Verilog
module control (
  input  [4:0] op,
  input  stall,
  input  clock,
  input  skip_n,
  output [2:0] aluop,
  output [2:0] cond,
  output skip,
  output halt,
  output error,
  output en_write,
  output mem,
  output store,
  output en_fetch,
  output jump,
  output write,
  output [1:0] wrmux
);

  wire [15:0] Microcode_d;

  ROM #(.AddrBits(5), .Bits(16)) Microcode (
    .A(op), .sel(1'b1),
    .D({Microcode_d[15:14], cond, wrmux, write, store, mem, aluop, jump, Microcode_d[1:0]}));
  and and_1 (halt, en_write, Microcode_d[0]);
  and and_2 (error, Microcode_d[1], en_write);
  Register u_skip (.D(skip_n), .C(clock), .en(en_fetch), .Q(skip));
  not not_1 (en_fetch, stall);
  and and_3 (en_write, ~skip, en_fetch);  // And

  // Other names for the same wires on the sheet: en_halt = en_write; en_skip = en_fetch

  // Notes on the sheet:
  //   contents of Microcode (hex, n*v repeats v):
  //   0,0,2,1,34,0,700,0,0,4,304,0,540,c0,540,c0,100,108,100,108,128,130,138,118,110,120,
  //   808,1008,1808,2008,2808,3008
  //   Halt Logic
  //   Skip Logic
  //   Stall Logic
endmodule

/* Test case ALU Ops:
op      stall aluop jump halt error mem store write wrmux
0b10000 0     0     0    0    0     0   0     1     0
0b01000 0     0     0    0    0     0   0     0     0
0b10110 0     2     0    0    0     0   0     1     0
0b01011 0     0     0    0    0     0   0     0     0
0b10110 1     2     0    0    0     0   0     1     0
0b10001 1     1     0    0    0     0   0     1     0
*/

/* Test case Halt:
op      stall clock skip_n aluop jump halt error mem store

# with stall and skip clear
0b00010 0     0     0      0     0    0    1     0   0
0b00011 0     0     0      0     0    1    0     0   0

# with skip set
0b00010 0     1     1      0     0    0    0     0   0
0b00011 0     1     1      0     0    0    0     0   0

# reset skip
0b00011 0     0     0      0     0    0    0     0   0
0b00011 0     1     0      0     0    1    0     0   0

# check stall
0b00010 1     0     0      0     0    0    0     0   0
0b00011 1     0     0      0     0    0    0     0   0
0b00010 1     1     1      0     0    0    0     0   0
0b00011 1     1     1      0     0    0    0     0   0
*/

/* Test case Jump:
op      stall clock skip_n aluop jump en_fetch halt error mem store
0b11100 0     0     0      0     1    1        0    0     0   0

# stalled
0b11100 1     0     0      0     1    0        0    0     0   0
*/

/* Test case Mem Access:
op      stall aluop jump halt error mem store write wrmux

0b11110 0     0     0    0    0     1   0     1     2 
0b11111 0     0     0    0    0     1   1     0     0

0b11110 1     0     0    0    0     1   0     1     2
0b11111 1     0     0    0    0     1   1     0     0
*/

/* Test case Skip:
op      stall clock skip_n skip en_write en_fetch
0b00000 0     0     0      0    1        1

# skip stays low when stalled
0b00000 1     0     1      0    0        0
0b00000 1     1     1      0    0        0

# skip updates when stall goes low
0b00000 0     0     1      0    1        1
0b00000 0     1     1      1    0        1

# skip stays high when stalled
0b00000 1     0     0      1    0        0
0b00000 1     1     0      1    0        0

# skip stays high if kept high with skip_n
0b00000 0     0     1      1    0        1
0b00000 0     1     1      1    0        1

# skip goes back low after skip_n goes low
0b00000 0     0     0      1    0        1
0b00000 0     1     0      0    1        1
*/
