// Digital circuit decoder.dig as structural Verilog
module decoder (
  input  [31:0] rdval,
  input  [31:0] rsval,
  input  [15:0] instr,
  output [1:0] rs,
  output [1:0] rd,
  output [1:0] result_mux,
  output [31:0] L,
  output [31:0] R,
  output tworeg,
  output move,
  output add,
  output [2:0] op,
  output jump
);

  wire [31:0] bitextender_1_out;

  BitExtender #(.outputBits(32)) bitextender_1 (.in(instr[15:8]), .out(bitextender_1_out));
  Multiplexer #(.Bits(32)) multiplexer_1 (.sel(instr[0]), .in_0(bitextender_1_out), .in_1(rsval), .out(R));
  Decoder #(.Selector_Bits(3)) decoder_1 (
    .sel(instr[3:1]), .out_0(add), .out_6(move), .out_7(jump));  // open: out_1, out_2, out_3, out_4, out_5
  PriorityEncoder #(.Selector_Bits(2)) priorityencoder_1 (
    .in0(jump), .in1(add), .in2(move), .in3(1'b0), .num(result_mux));  // open: any

  assign L = rdval;
  assign op = instr[3:1];
  assign rd = instr[5:4];
  assign rs = instr[7:6];
  assign tworeg = instr[0];
endmodule
