// Digital circuit execute.dig as structural Verilog
module execute (
  input  [15:0] L,
  input  [15:0] R,
  input  [2:0] cond,
  input  [2:0] op,
  output [15:0] result,
  output skip_n
);

  wire and_1_out, and_2_out, and_3_out, and_4_out, and_5_out, and_6_out, eq, ge, hs, lo, lt, ne, not_1_out,
       or_1_out, or_2_out, signed_eq, signed_gt, signed_lt, unsigned_eq, unsigned_gt, unsigned_lt;
  wire [15:0] add_1_s;

  Decoder #(.Selector_Bits(3)) decoder_1 (
    .sel(cond), .out_1(eq), .out_2(ne), .out_3(lt), .out_4(ge), .out_5(lo), .out_6(hs));  // open: out_0, out_7
  Add #(.Bits(16)) add_1 (.a(L), .b(R), .c_i(1'b0), .s(add_1_s));  // open: c_o
  Comparator #(.Signed("true"), .Bits(16)) \signed  (.a(L), .b(R), .gt(signed_gt), .eq(signed_eq), .lt(signed_lt));
  Comparator #(.Bits(16)) \unsigned  (.a(L), .b(R), .gt(unsigned_gt), .eq(unsigned_eq), .lt(unsigned_lt));
  or or_1 (or_1_out, signed_gt, signed_eq);
  or or_2 (or_2_out, unsigned_gt, unsigned_eq);
  not not_1 (not_1_out, signed_eq);
  Multiplexer #(.Selector_Bits(3), .Bits(16)) multiplexer_1 (
    .sel(op), .in_0(add_1_s), .in_1({16{1'b0}}), .in_2({16{1'b0}}), .in_3({16{1'b0}}), .in_4(L), .in_5(L),
    .in_6(R), .in_7(L), .out(result));
  and and_1 (and_1_out, lt, or_1_out);
  and and_2 (and_2_out, ne, signed_eq);
  and and_3 (and_3_out, eq, not_1_out);
  and and_4 (and_4_out, ge, signed_lt);
  and and_5 (and_5_out, lo, or_2_out);
  and and_6 (and_6_out, hs, unsigned_lt);
  or or_3 (skip_n, and_1_out, and_2_out, and_3_out, and_4_out, and_5_out, and_6_out);
endmodule
