// Digital circuit frontpanel.dig as structural Verilog
module frontpanel (
  input  clock,
  input  erun,
  input  DC,
  output [15:0] R0,
  output [15:0] R1,
  output [15:0] R2,
  output [15:0] R3,
  output [15:0] PC,
  output halt,
  output error
);

  wire aluopdisplay_1_p1, aluopdisplay_1_p2, busdisplay_1_p1, busdisplay_1_p2, busdisplay_1_p3,
       busdisplay_1_p4, busdisplay_1_p5, busdisplay_2_p1, busdisplay_2_p2, busdisplay_2_p3, busdisplay_2_p4,
       busdisplay_2_p5, busdisplay_3_p1, busdisplay_3_p2, busdisplay_3_p3, busdisplay_3_p4, busdisplay_3_p5,
       busdisplay_4_p1, busdisplay_4_p2, busdisplay_4_p3, busdisplay_4_p4, busdisplay_4_p5, dipswitch_1_out,
       hex, instrdisplay_1_p1, instrdisplay_1_p2, instrdisplay_1_p3, instrdisplay_1_p4, instrdisplay_1_p5,
       instrdisplay_1_p6, MC, rddisplay_1_p1, rddisplay_1_p2, rddisplay_2_p1, rddisplay_2_p2, rj32_1_w_en,
       rsdisplay_1_p1, rsdisplay_1_p2, run_t, skip, slow_t, stalled_t, step_t;
  wire [3:0] busdisplay_1_d1, busdisplay_1_d2, busdisplay_1_d3, busdisplay_1_d4, busdisplay_1_d5,
       busdisplay_2_d1, busdisplay_2_d2, busdisplay_2_d3, busdisplay_2_d4, busdisplay_2_d5, busdisplay_3_d1,
       busdisplay_3_d2, busdisplay_3_d3, busdisplay_3_d4, busdisplay_3_d5, busdisplay_4_d1, busdisplay_4_d2,
       busdisplay_4_d3, busdisplay_4_d4, busdisplay_4_d5;
  wire [7:0] rj32_1_a_prog;
  wire [13:0] rj32_1_a_data;
  wire [15:0] aluopdisplay_1_d1, aluopdisplay_1_d2, Data_d, instrdisplay_1_d1, instrdisplay_1_d2,
       instrdisplay_1_d3, instrdisplay_1_d4, instrdisplay_1_d5, instrdisplay_1_d6, Program_d, rddisplay_1_d1,
       rddisplay_1_d2, rddisplay_2_d1, rddisplay_2_d2, rj32_1_d_out, rsdisplay_1_d1, rsdisplay_1_d2;
  wire [25:0] aluopdisplay_1_o, busdisplay_1_o, busdisplay_2_o, db, rddisplay_1_o, rddisplay_2_o,
       rsdisplay_1_o, undriven, undriven_2, undriven_3, undriven_4, undriven_5;

  BlockRAMDualPort #(.AddrBits(8), .isProgramMemory("true"), .Bits(16)) Program (
    .A(rj32_1_a_prog), .Din({16{1'b0}}), .str(1'b0), .C(MC), .D(Program_d));
  BlockRAMDualPort #(.AddrBits(14), .Bits(16)) Data (
    .A(rj32_1_a_data), .Din(rj32_1_d_out), .str(rj32_1_w_en), .C(MC), .D(Data_d));
  Button step (.out(step_t));
  Button slow (.out(slow_t));
  Button run (.out(run_t));
  LED stalled (.in(stalled_t));
  SixteenSeg sixteenseg_1 (.led(rddisplay_1_d1), .dp(rddisplay_1_p1));
  SixteenSeg sixteenseg_2 (.led(rddisplay_1_d2), .dp(rddisplay_1_p2));
  rddisplay rddisplay_1 (
    .D1(rddisplay_1_d1), .P1(rddisplay_1_p1), .D2(rddisplay_1_d2), .P2(rddisplay_1_p2), .i(db),
    .o(rddisplay_1_o), .C(1'b0));
  rj32 rj32_1 (
    .stall(stalled_t), .skip(skip), .halt(halt), .error(error), .db(db), .erun(erun), .run_faster(1'b1),
    .run_fast(run_t), .run_slow(slow_t), .step(step_t), .clock(clock), .clock_m(MC), .A_prog(rj32_1_a_prog),
    .D_prog(Program_d), .w_en(rj32_1_w_en), .D_out(rj32_1_d_out), .A_data(rj32_1_a_data), .D_in(Data_d));
  SixteenSeg sixteenseg_3 (.led(instrdisplay_1_d1), .dp(instrdisplay_1_p1));
  SixteenSeg sixteenseg_4 (.led(instrdisplay_1_d2), .dp(instrdisplay_1_p2));
  instrdisplay instrdisplay_1 (
    .D1(instrdisplay_1_d1), .P1(instrdisplay_1_p1), .D2(instrdisplay_1_d2), .P2(instrdisplay_1_p2),
    .D3(instrdisplay_1_d3), .P3(instrdisplay_1_p3), .D4(instrdisplay_1_d4), .P4(instrdisplay_1_p4),
    .D5(instrdisplay_1_d5), .P5(instrdisplay_1_p5), .D6(instrdisplay_1_d6), .P6(instrdisplay_1_p6));  // open: I
  Seven_Seg_Hex seven_seg_hex_1 (.d(busdisplay_1_d1), .dp(busdisplay_1_p1));
  Seven_Seg_Hex seven_seg_hex_2 (.d(busdisplay_1_d2), .dp(busdisplay_1_p2));
  busdisplay busdisplay_1 (
    .D1(busdisplay_1_d1), .P1(busdisplay_1_p1), .D2(busdisplay_1_d2), .P2(busdisplay_1_p2),
    .D3(busdisplay_1_d3), .P3(busdisplay_1_p3), .D4(busdisplay_1_d4), .P4(busdisplay_1_p4),
    .D5(busdisplay_1_d5), .P5(busdisplay_1_p5), .i(rddisplay_1_o), .o(busdisplay_1_o), .C(2'b11), .H(hex));
  SixteenSeg sixteenseg_5 (.led(instrdisplay_1_d3), .dp(instrdisplay_1_p3));
  SixteenSeg sixteenseg_6 (.led(instrdisplay_1_d4), .dp(instrdisplay_1_p4));
  Seven_Seg_Hex seven_seg_hex_3 (.d(busdisplay_1_d3), .dp(busdisplay_1_p3));
  Seven_Seg_Hex seven_seg_hex_4 (.d(busdisplay_1_d4), .dp(busdisplay_1_p4));
  SixteenSeg sixteenseg_7 (.led(instrdisplay_1_d5), .dp(instrdisplay_1_p5));
  SixteenSeg sixteenseg_8 (.led(instrdisplay_1_d6), .dp(instrdisplay_1_p6));
  Seven_Seg_Hex seven_seg_hex_5 (.d(busdisplay_1_d5), .dp(busdisplay_1_p5));
  SixteenSeg sixteenseg_9 (.led(rddisplay_2_d1), .dp(rddisplay_2_p1));
  rddisplay rddisplay_2 (
    .D1(rddisplay_2_d1), .P1(rddisplay_2_p1), .D2(rddisplay_2_d2), .P2(rddisplay_2_p2), .i(undriven),
    .o(rddisplay_2_o), .C(1'b1));
  Seven_Seg_Hex seven_seg_hex_6 (.d(busdisplay_2_d1), .dp(busdisplay_2_p1));
  Seven_Seg_Hex seven_seg_hex_7 (.d(busdisplay_2_d2), .dp(busdisplay_2_p2));
  busdisplay busdisplay_2 (
    .D1(busdisplay_2_d1), .P1(busdisplay_2_p1), .D2(busdisplay_2_d2), .P2(busdisplay_2_p2),
    .D3(busdisplay_2_d3), .P3(busdisplay_2_p3), .D4(busdisplay_2_d4), .P4(busdisplay_2_p4),
    .D5(busdisplay_2_d5), .P5(busdisplay_2_p5), .i(busdisplay_1_o), .o(busdisplay_2_o), .C(2'b01), .H(hex));
  SixteenSeg sixteenseg_10 (.led(rddisplay_2_d2), .dp(rddisplay_2_p2));
  Seven_Seg_Hex seven_seg_hex_8 (.d(busdisplay_2_d3), .dp(busdisplay_2_p3));
  Seven_Seg_Hex seven_seg_hex_9 (.d(busdisplay_2_d4), .dp(busdisplay_2_p4));
  SixteenSeg sixteenseg_11 (.led(rsdisplay_1_d1), .dp(rsdisplay_1_p1));
  SixteenSeg sixteenseg_12 (.led(rsdisplay_1_d2), .dp(rsdisplay_1_p2));
  rsdisplay rsdisplay_1 (
    .D1(rsdisplay_1_d1), .P1(rsdisplay_1_p1), .D2(rsdisplay_1_d2), .P2(rsdisplay_1_p2), .i(rddisplay_2_o),
    .o(rsdisplay_1_o));
  Seven_Seg_Hex seven_seg_hex_10 (.d(busdisplay_2_d5), .dp(busdisplay_2_p5));
  DipSwitch dipswitch_1 (.out(dipswitch_1_out));
  Seven_Seg_Hex seven_seg_hex_11 (.d(busdisplay_3_d1), .dp(busdisplay_3_p1));
  busdisplay busdisplay_3 (
    .D1(busdisplay_3_d1), .P1(busdisplay_3_p1), .D2(busdisplay_3_d2), .P2(busdisplay_3_p2),
    .D3(busdisplay_3_d3), .P3(busdisplay_3_p3), .D4(busdisplay_3_d4), .P4(busdisplay_3_p4),
    .D5(busdisplay_3_d5), .P5(busdisplay_3_p5), .i(rsdisplay_1_o), .C(2'b00), .H(hex));  // open: o
  SixteenSeg sixteenseg_13 (.led(aluopdisplay_1_d1), .dp(aluopdisplay_1_p1));
  SixteenSeg sixteenseg_14 (.led(aluopdisplay_1_d2), .dp(aluopdisplay_1_p2));
  aluopdisplay aluopdisplay_1 (
    .D1(aluopdisplay_1_d1), .P1(aluopdisplay_1_p1), .D2(aluopdisplay_1_d2), .P2(aluopdisplay_1_p2),
    .i(busdisplay_2_o), .o(aluopdisplay_1_o));
  // vga_frontpanel vga_frontpanel_1: pin names not known; wires that end beside it: DC, dipswitch_1_out, db
  Seven_Seg_Hex seven_seg_hex_12 (.d(busdisplay_3_d2), .dp(busdisplay_3_p2));
  Seven_Seg_Hex seven_seg_hex_13 (.d(busdisplay_3_d3), .dp(busdisplay_3_p3));
  Seven_Seg_Hex seven_seg_hex_14 (.d(busdisplay_4_d1), .dp(busdisplay_4_p1));
  Seven_Seg_Hex seven_seg_hex_15 (.d(busdisplay_3_d4), .dp(busdisplay_3_p4));
  Seven_Seg_Hex seven_seg_hex_16 (.d(busdisplay_3_d5), .dp(busdisplay_3_p5));
  DipSwitch u_hex (.out(hex));
  Seven_Seg_Hex seven_seg_hex_17 (.d(busdisplay_4_d2), .dp(busdisplay_4_p2));
  Seven_Seg_Hex seven_seg_hex_18 (.d(busdisplay_4_d3), .dp(busdisplay_4_p3));
  busdisplay busdisplay_4 (
    .D1(busdisplay_4_d1), .P1(busdisplay_4_p1), .D2(busdisplay_4_d2), .P2(busdisplay_4_p2),
    .D3(busdisplay_4_d3), .P3(busdisplay_4_p3), .D4(busdisplay_4_d4), .P4(busdisplay_4_p4),
    .D5(busdisplay_4_d5), .P5(busdisplay_4_p5), .i(aluopdisplay_1_o), .C(2'b10), .H(hex));  // open: o
  Seven_Seg_Hex seven_seg_hex_19 (.d(busdisplay_4_d4), .dp(busdisplay_4_p4));
  Seven_Seg_Hex seven_seg_hex_20 (.d(busdisplay_4_d5), .dp(busdisplay_4_p5));
  debugreg debugreg_1 (.i(db), .s(8'h17), .v(PC), .o(undriven_2));
  debugreg debugreg_2 (.i(undriven_2), .s({8{1'b0}}), .v(R0), .o(undriven_3));
  debugreg debugreg_3 (.i(undriven_3), .s(8'h1), .v(R1), .o(undriven_4));
  debugreg debugreg_4 (.i(undriven_4), .s(8'h2), .v(R2), .o(undriven_5));
  debugreg debugreg_5 (.i(undriven_5), .s(8'h3), .v(R3));  // open: o
  LED u_skip (.in(skip));

  // Other names for the same wires on the sheet: C = clock

  // Notes on the sheet:
  //   clock: Hz: 1000
  //   DC: Hz: 2147483647
  //   rj45 Creates
  //   =
endmodule
