// Digital circuit rj32.dig as structural Verilog
module rj32 (
  input  clock,
  input  step,
  input  run_slow,
  input  [15:0] D_prog,
  input  [15:0] D_in,
  input  run_fast,
  input  run_faster,
  input  erun,
  output [15:0] R0,
  output [15:0] R1,
  output [15:0] R2,
  output [15:0] R3,
  output [15:0] PC,
  output halt,
  output error,
  output skip,
  output rd_valid,
  output rs_valid,
  output [4:0] op,
  output [2:0] cond,
  output stall,
  output [15:0] L,
  output [15:0] R,
  output [3:0] rd,
  output [3:0] rs,
  output jump,
  output [7:0] A_prog,
  output clock_m,
  output [13:0] A_data,
  output [15:0] D_out,
  output w_en,
  output [15:0] result,
  output immv,
  output [15:0] imm,
  output [2:0] aluop
);

  wire control_1_p10, control_1_p11, en, en_fetch, fetch_1_p7, regwrite_t, skip_n;
  wire [15:0] decoder_1_p1, decoder_1_p2, execute_1_result;

  not not_1 (clock_m, clock);
  // fetch fetch_1: pin names not known; wires that end beside it: result, D_prog, clock, en_fetch, jump, en, fetch_1_p7, {PC[15:8], A_prog}
  // decoder decoder_1: pin names not known; wires that end beside it: decoder_1_p1, decoder_1_p2, fetch_1_p7, {PC[15:8], A_prog}, jump, rs, rd, L, R, cond, op, rs_valid, rd_valid, imm, immv
  clockctrl clockctrl_1 (
    .clock(clock), .step(step), .slow(run_slow), .fast(run_fast), .faster(run_faster), .efast(erun),
    .stall(stall));
  // control control_1: pin names not known; wires that end beside it: op, stall, clock, skip_n, aluop, skip, halt, error, en, control_1_p10, control_1_p11, en_fetch, jump, regwrite_t
  execute execute_1 (.L(L), .R(R), .cond(cond), .op(aluop), .result(execute_1_result), .skip_n(skip_n));
  memaccess memaccess_1 (
    .result(execute_1_result), .rdval(decoder_1_p1), .mem(control_1_p10), .memop(control_1_p11), .D(D_in),
    .en(en), .wrval(result), .A(A_data), .str(w_en), .D_in(D_out));
  regfile regfile_1 (
    .rs(rs), .rd(rd), .result(result), .clock(clock), .en(en), .wr(regwrite_t), .rdval(decoder_1_p1),
    .rsval(decoder_1_p2), .R0(R0), .R1(R1), .R2(R2), .R3(R3));

  assign PC[7:0] = A_prog;

  // Other names for the same wires on the sheet: A_data_t[13:0] = A_data; aluop_t[2:0] = aluop; C = clock;
  //   cond_t[2:0] = cond; D_in_t[15:0] = D_in; D_out_t[15:0] = D_out; D_prog_t[15:0] = D_prog; error_t = error;
  //   halt_t = halt; imm_t[15:0] = imm; immv_t = immv; jump_t = jump; L_t[15:0] = L; op_t[4:0] = op;
  //   A_prog_t[15:0] = {PC[15:8], A_prog}; PC_t[15:0] = {PC[15:8], A_prog}; R_t[15:0] = R; rd_t[3:0] = rd;
  //   rdvalid_t = rd_valid; result_t[15:0] = result; rs_t[3:0] = rs; rsvalid_t = rs_valid; skip_t = skip;
  //   stall_t = stall; W_en_t = w_en

  // Notes on the sheet:
  //   clock: Hz: 10
  //   rj45 Creates
endmodule
