// Digital circuit testsuite.dig as structural Verilog
module testsuite (
  input  clock,
  input  run,
  output error,
  output halt,
  output [7:0] PC
);

  frontpanel frontpanel_1 (.clock(clock), .erun(run), .PC(PC), .halt(halt), .error(error));  // open: R0, R1, R2, R3
endmodule

/* Test case add:
clock run error halt

# #include "../cpudef.asm"
# 
# move r1, 5
# move r2, 3
# add r1, r2
# add r1, 2
# eq r1, 10
# halt

program(0x2b0b, 0x1b13, 0x810a, 0x100b, 0x520b, 0x0008)

let i = 0;
while(!(halt | error | (i >= 100)))
  let i = i + 1;
  0 1 0 0
  1 1 x x
end while
0 1 0 1
*/

/* Test case jump:
clock run error halt

# #include "../cpudef.asm"
# 
#   jump one
#   halt
# three:
#   add r0, r1
#   add r0, r2
#   jump end
#   halt
# two:
#   move r2, 2
#   jump three
#   halt
# one:
#   move r1, 3
#   jump two
#   halt
# end:
#   eq r0, 5
#   halt

program(0x0121, 0x0008, 0x8082, 0x8102, 0x0181, 0x0008, 0x1313, 0x0041, 0x0008, 0x1b0b, 0x00c1, 0x0008, 0x2a03, 0x0008)

let i = 0;
while(!(halt | error | (i >= 100)))
  let i = i + 1;
  0 1 0 0
  1 1 x x
end while
0 1 0 1
*/

/* Test case conditionals:
clock run error halt

# #include "../cpudef.asm"
# 
#   brt end
#   brf one
# three:
#   add r0, r1
#   add r0, r2
#   eq r2, 5
#   brt one
#   jump end
# two:
#   move r2, 2
#   eq r1, 5
#   brf three
# one:
#   move r1, 3
#   eq r1, 3
#   brt two
# end:
#   eq r0, 5
#   halt

program(0x01b1, 0x0159, 0x8082, 0x8102, 0x2a13, 0x0151, 0x01a1, 0x1313, 0x2a0b, 0x0059, 0x1b0b, 0x1a0b, 0x00f1, 0x2a03, 0x0008)

let i = 0;
while(!(halt | error | (i >= 100)))
  let i = i + 1;
  0 1 0 0
  1 1 x x
end while
0 1 0 1
*/

/* Test case loadstore:
clock run error halt

# #include "../cpudef.asm"
# 
# move r0, 2
# move r1, 5
# 
# ; memory doesn't have 5
# load r2, [r0,0]
# eq r2, 5
# brt fail
# 
# ; store and check it does have 5
# store [r0,0], r1
# load r2, [r0,0]
# eq r2, 5
# brf fail
# 
# ; check max offset of 31
# move r1, 7
# store [r0,31], r1
# load r2, [r0,31]
# eq r2, 7
# brf fail
# 
# ; check base equivalent to offset
# move r2, 0
# add r0, 15
# add r0, 15
# add r0, 1
# load r2, [r0, 0]
# eq r2, 7
# halt
# 
# fail:
# eq r0, 1
# halt

program(0x1303, 0x2b0b, 0x0014, 0x2a13, 0x02b1, 0x000d, 0x0014, 0x2a13, 0x02b9, 0x3b0b, 0xf80d, 0xf814, 0x3a13, 0x02b9, 0x0313, 0x7803, 0x7803, 0x0803, 0x0014, 0x3a13, 0x0008, 0x0a03, 0x0008)

let i = 0;
while(!(halt | error | (i >= 100)))
  let i = i + 1;
  0 1 0 0
  1 1 x x
end while
0 1 0 1
*/
