// Digital circuit vga_blinkenlights.dig as structural Verilog
module vga_blinkenlights (
  input  clock,
  input  [25:0] db,
  input  [11:0] res_H,
  input  [11:0] fp_H,
  input  [11:0] sync_H,
  input  [11:0] bp_H,
  input  neg_H,
  input  [11:0] res_V,
  input  [11:0] fp_V,
  input  [11:0] sync_V,
  input  [11:0] bp_V,
  input  neg_V,
  input  [15:0] TD,
  input  [7:0] MD,
  output [3:0] R,
  output [3:0] G,
  output [3:0] B,
  output hs,
  output vs,
  output de,
  output [10:0] TA,
  output [9:0] MA
);

  wire debugcopy_1_p4, debugrender_1_fb_valid, vb;
  wire [3:0] colour_d;
  wire [4:0] multiplexer_1_out, sub_1_s;
  wire [5:5] sub_1_s_2;
  wire [7:0] debugrender_1_fb_d, Frame_Buffer_d2, X, Y;
  wire [8:0] debugrender_1_fb_a;
  wire [21:0] debugcopy_1_p5;

  // debugcopy debugcopy_1: pin names not known; wires that end beside it: db, clock, vb, debugcopy_1_p4, debugcopy_1_p5
  Sub #(.Bits(6)) sub_1 (.a(X[5:0]), .b(6'b000100), .c_i(1'b0), .s({sub_1_s_2[5], sub_1_s}));  // open: c_o
  debugrender debugrender_1 (
    .db(debugcopy_1_p5), .clock(clock), .fb_valid(debugrender_1_fb_valid), .fb_A(debugrender_1_fb_a),
    .fb_D(debugrender_1_fb_d), .rdy(debugcopy_1_p4));
  Multiplexer #(.Bits(5)) multiplexer_1 (.sel(sub_1_s_2[5]), .in_0(sub_1_s), .in_1({5{1'b0}}), .out(multiplexer_1_out));
  RAMDualAccess #(.AddrBits(9), .Bits(8)) Frame_Buffer (
    .str(debugrender_1_fb_valid), .C(clock), .ld(1'b0), .A1(debugrender_1_fb_a), .Din1(debugrender_1_fb_d),
    .A2({Y[3:0], multiplexer_1_out}), .D2(Frame_Buffer_d2));  // open: D1
  ROM #(.AddrBits(9), .Bits(7)) fb (.A({Y[3:0], multiplexer_1_out}), .sel(1'b1));  // open: D
  ROM #(.AddrBits(9), .Bits(4)) colour (.A({Y[3:0], multiplexer_1_out}), .sel(1'b1), .D(colour_d));
  // vga_display vga_display_1: pin names not known; wires that end beside it: clock, res_H, fp_H, sync_H, bp_H, neg_H, res_V, fp_V, sync_V, bp_V, neg_V, Frame_Buffer_d2[6:0], colour_d, {12{1'b0}}, TD, MD, R, G, B, hs, vs, de, X, Y, vb, TA, MA

  // Other names for the same wires on the sheet: C = clock; resX[11:0] = res_H

  // Notes on the sheet:
  //   clock: Hz: 8000
  //   res_H: default 640
  //   fp_H: default 16
  //   sync_H: default 96
  //   bp_H: default 48
  //   res_V: default 400
  //   fp_V: default 12
  //   sync_V: default 2
  //   bp_V: default 35
  //   contents of fb (hex, n*v repeats v):
  //   0,0,0,0,0,0,0,0,0,0,0,0,0,0,0,0,0,0,0,0,0,0,0,0,0,0,0,0,0,0,0,0,0,2d,31,32,33,34,
  //   35,0,0,2d,31,32,33,34,35,0,0,2d,31,32,33,34,35,0,0,2d,31,32,33,34,35,0,0,2d,31,32,
  //   33,34,35,0,0,2d,31,32,33,34,35,0,0,2d,31,32,33,34,35,0,0,2d,31,32,33,34,35,0,0,2d,
  //   31,32,33,34,35,0,0,2d,31,32,33,34,35,0,0,2d,31,32,33,34,35,0,0,2d,31,32,33,34,35,
  //   0,0,2d,31,32,33,34,35,0,0,2d,31,32,33,34,35,0,0,2d,31,32,33,34,35,0,0,2d,31,32,33,
  //   34,35,0,0,0,0,0,0,0,0,0,0,0,0,0,0,0,0,0,0,0,0,0,0,0,0,0,0,0,0,0,0,0,0,0,0,41,42,43,
  //   44,45,46,47,48,0,0,0,52,31,35,2c,0,0,0,0,52,31,33,0,0,2d,31,32,33,34,35,0,0,0,0,0,
  //   0,0,0,0,0,0,0,0,0,0,0,0,0,0,0,0,0,0,0,0,0,0,0,0,0,0,0,0,0,52,31,35,0,0,3d,0,0,2d,
  //   31,32,33,34,35,0,3d,2d,31,32,33,34,35,0,2b,2d,31,32,33,34,35,0,0,0,0,0,0,0,0,0,0,
  //   0,0,0,0,0,0,0,0,0,0,0,0,0,0,0,0,0,0,0,0,0,0,0,0,2d,31,32,33,34,35,0,0,38,0,0,0,0,
  //   0,38,0,0,0,0,0,38,0,0,0,0,0,38
  //   contents of colour (hex, n*v repeats v):
  //   0,0,0,0,0,0,0,0,0,0,0,0,0,0,0,0,0,0,0,0,0,0,0,0,0,0,0,0,0,0,0,0,0,0,0,0,0,0,0,0,0,
  //   0,0,0,0,4,4,4,4,0,0,4,4,4,4,0,0,4,4,4,4,0,0,4,4,4,4,0,0,0,0,0,0,0,0,0,0,0,0,0,0,0,
  //   0,0,0,4,4,4,4,0,0,4,4,4,4,0,0,4,4,4,4,0,0,4,4,4,4,0,0,0,0,0,0,0,0,0,0,0,0,0,0,0,0,
  //   0,0,4,4,4,4,0,0,4,4,4,4,0,0,4,4,4,4,0,0,4,4,4,4,0,0,0,0,0,0,0,0,0,0,0,0,0,0,0,0,0,
  //   0,0,0,0,0,0,0,0,0,0,0,0,0,0,0,0,0,0,0,0,0,0,0,0,0,0,0,0,0,0,0,0,0,0,0,0,0,0,0,0,0,
  //   0,0,0,0,0,0,0,0,0,0,0,0,0,0,0,0,0,0,0,0,0,0,0,0,0,0,0,0,0,0,0,0,0,0,0,0,0,0,0,0,6,
  //   6,6,6,6,6,6,6,0,0,0,2,2,2,2,0,0,0,0,2,2,2,0,0,4,4,4,4,0,0,0,0,0,0,0,0,0,0,0,0,0,0,
  //   0,0,0,0,0,0,0,0,0,0,0,0,0,0,0,0,0,0,0,0,0,0,0,0,0,0,0,0,0,0,0,0,0,0,0,0,0,0,2,2,2,
  //   0,0,2,0,0,4,4,4,4,0,2,4,4,4,4,3,3,4,4,4,4,0,0,0,0,0,0,0,0,0,0,0,0,0,0,0,0,0,0,0,0,
  //   0,0,0,0,0,0,0,0,0,0,0,0,0,0,0,0,0,0,0,0,0,0,0,0,0,0,0,0,0,0,0,0,0,0,0,0,4,4,4,4,0,
  //   0,5,0,0,0,0,0,4,0,0,0,0,0,3,0,0,0,0,0,2
endmodule
