// Digital circuit vga_frontpanel.dig as structural Verilog
module vga_frontpanel (
  input  clock,
  input  [7:0] PC,
  input  [15:0] R0,
  input  [15:0] R1,
  input  [15:0] R2,
  input  [15:0] R3,
  input  en,
  input  [15:0] L,
  input  [15:0] R,
  input  [4:0] op,
  input  [2:0] cond,
  input  jump,
  input  skip,
  input  [15:0] result,
  input  clock_slow,
  input  [3:0] rs,
  input  [3:0] rd,
  input  rd_valid,
  input  rs_valid,
  input  halt,
  input  error,
  input  [15:0] imm,
  input  imm_valid,
  input  [2:0] aluop
);

  wire C, vga_blinkenlights_1_hs, vga_blinkenlights_1_vs;
  wire [3:0] vga_blinkenlights_1_b, vga_blinkenlights_1_g, vga_blinkenlights_1_r;
  wire [10:0] vga_blinkenlights_1_ca;
  wire [15:0] Char_ROM_d, d_ff_1_q;

  and and_1 (C, en, clock);
  vga_blinkenlights vga_blinkenlights_1 (
    .clock(C), .PC({{8{1'b0}}, PC}), .R0(R0), .R1(R1), .R2(R2), .R3(R3), .L_b(L), .R_b(R), .result(result),
    .skip(skip), .jump(jump), .op(op), .cond(cond), .rd(rd), .rs(rs), .rdv(rd_valid), .rsv(rs_valid),
    .halt(halt), .error(error), .imm(imm), .immv(imm_valid), .aluop(aluop), .clock_slow(clock_slow),
    .CD(d_ff_1_q), .R(vga_blinkenlights_1_r), .G(vga_blinkenlights_1_g), .B(vga_blinkenlights_1_b),
    .hs(vga_blinkenlights_1_hs), .vs(vga_blinkenlights_1_vs), .CA(vga_blinkenlights_1_ca));  // open: PD, de, PA
  VGA vga_1 (
    .R(vga_blinkenlights_1_r), .G(vga_blinkenlights_1_g), .B(vga_blinkenlights_1_b),
    .H(vga_blinkenlights_1_hs), .V(vga_blinkenlights_1_vs), .C(C));
  ROM #(.AddrBits(11), .Bits(16)) Char_ROM (.A(vga_blinkenlights_1_ca), .sel(1'b1), .D(Char_ROM_d));
  D_FF #(.Bits(16)) d_ff_1 (.D(Char_ROM_d), .C(C), .Q(d_ff_1_q));  // open: nQ

  // Other names for the same wires on the sheet: aluop_t[2:0] = aluop; cond_t[2:0] = cond; error_t = error;
  //   halt_t = halt; imm_t[15:0] = imm; imv_t = imm_valid; jump_t = jump; L_t[15:0] = L; op_t[4:0] = op;
  //   PC_t[7:0] = PC; R0_t[15:0] = R0; R1_t[15:0] = R1; R2_t[15:0] = R2; R3_t[15:0] = R3; R_t[15:0] = R;
  //   rd_t[3:0] = rd; rdv_t = rd_valid; result_t[15:0] = result; rs_t[3:0] = rs; rsv_t = rs_valid; SC = clock_slow;
  //   skip_t = skip

  // Notes on the sheet:
  //   clock: Hz: 2147483647
  //   contents of Char_ROM (hex, n*v repeats v):
  //   0,0,0,0,0,0,0,0,0,0,0,0,0,0,0,0,0,0,0,0,0,0,0,0,0,0,0,0,0,0,0,0,0,0,0,180,180,180,
  //   180,180,180,180,180,0,0,180,180,180,180,180,180,180,180,0,0,0,0,0,0,0,0,0,0,0,0,3e7c,
  //   1e78,0,0,0,0,0,0,0,0,0,0,0,0,0,0,0,0,0,0,0,0,0,0,0,0,0,0,0,0,0,0,3e7c,3ffc,4182,6186,
  //   6186,6186,6186,6186,6186,4182,3e7c,3e7c,4182,6186,6186,6186,6186,6186,6186,4182,3ffc,
  //   3e7c,0,0,0,0,0,0,0,0,0,0,3e7c,3ff8,4180,6180,6180,6180,6180,6180,6180,4180,3e7c,3e7c,
  //   182,186,186,186,186,186,186,182,1ffc,3e7c,0,0,0,0,0,0,0,0,0,0,3e00,3f00,4188,6188,
  //   6198,61b0,61b0,61e0,61e0,4180,3e7c,3e7c,182,786,786,d86,d86,1986,1186,1182,fc,7c,
  //   0,0,0,0,0,0,0,0,0,0,3e00,3f00,4180,6180,6180,6180,6180,6180,6180,4180,3f00,3e00,4000,
  //   6060,6060,6030,6030,6018,6008,4000,3e78,3e7c,0,0,0,0,0,0,0,0,0,0,0,0,8,8,18,30,30,
  //   60,60,0,0,0,0,0,0,0,0,0,0,0,0,0,0,0,0,0,0,0,0,0,0,0,7c,78,200,600,600,c00,800,1800,
  //   1000,0,0,0,0,1000,1800,800,c00,600,600,200,78,7c,0,0,0,0,0,0,0,0,0,0,3e00,1e00,40,
  //   60,60,30,10,18,8,0,0,0,0,8,18,10,30,60,60,40,1e00,3e00,0,0,0,0,0,0,0,0,0,0,0,0,1188,
  //   1188,1998,db0,db0,7e0,7e0,180,3e7c,3e7c,180,7e0,7e0,db0,db0,1998,1188,1188,0,0,0,
  //   0,0,0,0,0,0,0,0,0,0,0,180,180,180,180,180,180,180,180,3e7c,3e7c,180,180,180,180,180,
  //   180,180,180,0,0,0,0,0,0,0,0,0,0,0,0,0,0,0,0,0,0,0,0,0,0,0,0,0,600,600,c00,c00,1800,
  //   1000,1000,0,0,0,0,0,0,0,0,0,0,0,0,0,0,0,0,0,0,0,0,0,0,3e7c,3e7c,0,0,0,0,0,0,0,0,0,
  //   0,0,0,0,0,0,0,0,0,0,0,0,0,0,0,0,0,0,0,0,0,0,0,0,0,0,0,0,0,0,0,180,180,0,0,0,0,0,0,
  //   0,0,0,0,0,0,8,8,18,30,30,60,60,0,0,0,0,600,600,c00,c00,1800,1000,1000,0,0,0,0,0,0,
  //   0,0,0,0,0,0,3e7c,3e7c,4006,600e,601a,6032,6036,6066,6066,6006,0,0,6006,6606,6606,
  //   6c06,4c06,5806,7006,6002,3e7c,3e7c,0,0,0,0,0,0,0,0,0,0,3e00,1f00,180,180,180,180,
  //   180,180,180,180,0,0,180,180,180,180,180,180,180,180,1ff8,3e7c,0,0,0,0,0,0,0,0,0,0,
  //   3e7c,1e7c,2,6,6,6,6,6,6,2,3e7c,3e7c,4000,6000,6000,6000,6000,6000,6000,4000,3e78,
  //   3e7c,0,0,0,0,0,0,0,0,0,0,3e7c,1e7c,2,6,6,6,6,6,6,2,3e7c,3e7c,2,6,6,6,6,6,6,2,1e7c,
  //   3e7c,0,0,0,0,0,0,0,0,0,0,0,4002,6006,6006,6006,6006,6006,6006,6006,4002,3e7c,3e7c,
  //   2,6,6,6,6,6,6,6,2,0,0,0,0,0,0,0,0,0,0,0,3e7c,3e78,4000,6000,6000,6000,6000,6000,6000,
  //   4000,3e7c,3e7c,2,6,6,6,6,6,6,2,1e7c,3e7c,0,0,0,0,0,0,0,0,0,0,3e7c,3e78,4000,6000,
  //   6000,6000,6000,6000,6000,4000,3e7c,3e7c,4002,6006,6006,6006,6006,6006,6006,4002,3e7c,
  //   3e7c,0,0,0,0,0,0,0,0,0,0,3e7c,1e7c,2,6,6,6,6,6,6,6,0,0,6,6,6,6,6,6,6,6,2,0,0,0,0,
  //   0,0,0,0,0,0,0,3e7c,3e7c,4002,6006,6006,6006,6006,6006,6006,4002,3e7c,3e7c,4002,6006,
  //   6006,6006,6006,6006,6006,4002,3e7c,3e7c,0,0,0,0,0,0,0,0,0,0,3e7c,3e7c,4002,6006,6006,
  //   6006,6006,6006,6006,4002,3e7c,3e7c,2,6,6,6,6,6,6,2,1e7c,3e7c,0,0,0,0,0,0,0,0,0,0,
  //   0,0,0,0,0,180,180,0,0,0,0,0,0,0,0,180,180,0,0,0,0,0,0,0,0,0,0,0,0,0,0,0,0,0,180,180,
  //   180,180,180,180,180,180,0,0,0,600,600,c00,c00,1800,1000,1000,0,0,0,0,0,0,0,0,0,0,
  //   0,0,0,0,40,c0,c0,180,180,300,300,0,0,0,0,300,300,180,180,c0,c0,40,0,0,0,0,0,0,0,0,
  //   0,0,0,0,0,0,0,0,0,3e7c,3e7c,0,0,0,0,0,0,0,0,1e78,3e7c,0,0,0,0,0,0,0,0,0,0,0,0,0,0,
  //   0,0,0,200,300,300,180,180,c0,c0,0,0,0,0,c0,c0,180,180,300,300,200,0,0,0,0,0,0,0,0,
  //   0,0,0,0,3e7c,1e7c,2,6,6,6,6,6,6,2,7c,fc,180,180,180,180,180,180,180,180,0,0,0,0,0,
  //   0,0,0,0,0,0,0,3e7c,3ffc,4182,6186,6186,6186,6186,6186,6186,6182,fc,7c,6000,6000,6000,
  //   6000,6000,6000,6000,4000,3e78,3e7c,0,0,0,0,0,0,0,0,0,0,3e7c,3e7c,4002,6006,6006,6006,
  //   6006,6006,6006,4002,3e7c,3e7c,4002,6006,6006,6006,6006,6006,6006,6006,4002,0,0,0,
  //   0,0,0,0,0,0,0,0,3e7c,1ffc,182,186,186,186,186,186,186,182,3e7c,3e7c,182,186,186,186,
  //   186,186,186,182,1ffc,3e7c,0,0,0,0,0,0,0,0,0,0,3e7c,3e78,4000,6000,6000,6000,6000,
  //   6000,6000,6000,0,0,6000,6000,6000,6000,6000,6000,6000,4000,3e78,3e7c,0,0,0,0,0,0,
  //   0,0,0,0,3e7c,1ffc,182,186,186,186,186,186,186,186,0,0,186,186,186,186,186,186,186,
  //   182,1ffc,3e7c,0,0,0,0,0,0,0,0,0,0,3e7c,3e78,4000,6000,6000,6000,6000,6000,6000,4000,
  //   3e7c,3e7c,4000,6000,6000,6000,6000,6000,6000,4000,3e78,3e7c,0,0,0,0,0,0,0,0,0,0,3e7c,
  //   3e78,4000,6000,6000,6000,6000,6000,6000,4000,3e7c,3e7c,4000,6000,6000,6000,6000,6000,
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endmodule
